// Logisim project ALU.circ as structural Verilog: 1 circuit, main circuit ALU
module ALU (
  input  [7:0] Input_Data,
  input  Operation,
  output [7:0] Result
);

  Multiplexer #(.width(8)) multiplexer_1 (
    .in0({Input_Data[6:0], Input_Data[7]}), .in1({Input_Data[0], Input_Data[7:1]}), .out(Result),
    .sel(Operation));  // open: en
endmodule
